// Logisim project 4 bit adder.circ as structural Verilog: 1 circuit, main circuit main
module main (
  input  in_1,
  input  in_2,
  input  in_3,
  input  in_4,
  input  in_5,
  input  in_6,
  input  in_7,
  input  in_8,
  output out_9,
  output out_10,
  output out_11,
  output out_12
);

  wire nand_1_out, nand_2_out, nand_3_out, nand_4_out, nand_5_out, nand_6_out, nand_7_out, nand_8_out,
       nand_10_out, nand_11_out, nand_12_out, nand_13_out, nand_14_out, nand_15_out, nand_16_out,
       nand_17_out, nand_18_out, nand_19_out, nand_20_out, nand_21_out, nand_22_out, nand_24_out,
       nand_25_out, nand_26_out, nand_27_out, nand_28_out, nand_30_out;

  nand nand_1 (nand_1_out, in_4, in_8);
  nand nand_2 (nand_2_out, in_3, in_7);
  nand nand_3 (nand_3_out, in_4, nand_1_out);
  nand nand_4 (nand_4_out, nand_1_out, in_8);
  nand nand_5 (nand_5_out, in_3, nand_2_out);
  nand nand_6 (nand_6_out, nand_2_out, in_7);
  nand nand_7 (nand_7_out, in_2, in_6);
  nand nand_8 (nand_8_out, in_1, in_5);
  nand nand_9 (out_12, nand_3_out, nand_4_out);
  nand nand_10 (nand_10_out, nand_1_out, nand_1_out);
  nand nand_11 (nand_11_out, nand_5_out, nand_6_out);
  nand nand_12 (nand_12_out, in_2, nand_7_out);
  nand nand_13 (nand_13_out, nand_7_out, in_6);
  nand nand_14 (nand_14_out, in_1, nand_8_out);
  nand nand_15 (nand_15_out, nand_8_out, in_5);
  nand nand_16 (nand_16_out, nand_11_out, nand_10_out);
  nand nand_17 (nand_17_out, nand_11_out, nand_16_out);
  nand nand_18 (nand_18_out, nand_16_out, nand_10_out);
  nand nand_19 (nand_19_out, nand_12_out, nand_13_out);
  nand nand_20 (nand_20_out, nand_14_out, nand_15_out);
  nand nand_21 (nand_21_out, nand_19_out, nand_24_out);
  nand nand_22 (nand_22_out, nand_20_out, nand_30_out);
  nand nand_23 (out_11, nand_17_out, nand_18_out);
  nand nand_24 (nand_24_out, nand_16_out, nand_2_out);
  nand nand_25 (nand_25_out, nand_19_out, nand_21_out);
  nand nand_26 (nand_26_out, nand_21_out, nand_24_out);
  nand nand_27 (nand_27_out, nand_20_out, nand_22_out);
  nand nand_28 (nand_28_out, nand_22_out, nand_30_out);
  nand nand_29 (out_10, nand_25_out, nand_26_out);
  nand nand_30 (nand_30_out, nand_21_out, nand_7_out);
  nand nand_31 (out_9, nand_27_out, nand_28_out);
  // NAND_Gate nand_32 has open pins: in0=nand_22_out, in1=nand_8_out, out=open
endmodule
