// Logisim project NibbleTo7Seg.circ as structural Verilog
module NibbleTo7SegmentDislay (
  input  [3:0] in
);

  wire A_B_C_D_out, A_B_CD_out, A_BC_D_out, A_BCD_out, AB_C_D_out, AB_CD_out, ABC_D_out, ABCD_out, BL_out,
       Bottom_out, BR_out, Middle_out, nA_B_C_D_out, nA_B_CD_out, nA_BC_D_out, nA_BCD_out, nAB_C_D_out,
       nAB_CD_out, nABC_D_out, nABCD_out, not_1_out, not_2_out, not_3_out, not_4_out, TL_out, Top_out, TR_out;

  not not_1 (not_1_out, in[3]);
  not not_2 (not_2_out, in[2]);
  not not_3 (not_3_out, in[0]);
  not not_4 (not_4_out, in[1]);
  and nA_B_C_D (nA_B_C_D_out, not_3_out, not_4_out, not_2_out, not_1_out);
  and A_B_C_D (A_B_C_D_out, in[0], not_4_out, not_2_out, not_1_out);
  and nAB_C_D (nAB_C_D_out, not_3_out, in[1], not_2_out, not_1_out);
  and AB_C_D (AB_C_D_out, in[0], in[1], not_2_out, not_1_out);
  and nA_BC_D (nA_BC_D_out, not_3_out, not_4_out, in[2], not_1_out);
  and A_BC_D (A_BC_D_out, in[0], not_4_out, in[2], not_1_out);
  and nABC_D (nABC_D_out, not_3_out, in[1], in[2], not_1_out);
  and ABC_D (ABC_D_out, in[0], in[1], in[2], not_1_out);
  and nA_B_CD (nA_B_CD_out, not_3_out, not_4_out, not_2_out, in[3]);
  and A_B_CD (A_B_CD_out, in[0], not_4_out, not_2_out, in[3]);
  and nAB_CD (nAB_CD_out, not_3_out, in[1], not_2_out, in[3]);
  and AB_CD (AB_CD_out, in[0], in[1], not_2_out, in[3]);
  and nA_BCD (nA_BCD_out, not_3_out, not_4_out, in[2], in[3]);
  and A_BCD (A_BCD_out, in[0], not_4_out, in[2], in[3]);
  and nABCD (nABCD_out, not_3_out, in[1], in[2], in[3]);
  and ABCD (ABCD_out, in[0], in[1], in[2], in[3]);
  nor Top (Top_out, A_B_C_D_out, nA_BC_D_out, AB_CD_out, nA_BCD_out, A_BCD_out);
  nor Middle (Middle_out, nA_B_C_D_out, A_B_C_D_out, ABC_D_out);
  nor Bottom (Bottom_out, A_B_C_D_out, nA_BC_D_out, ABC_D_out, nAB_CD_out, ABCD_out);
  nor TL (TL_out, A_B_C_D_out, nAB_C_D_out, AB_C_D_out, ABC_D_out, nA_BCD_out, A_BCD_out);
  nor TR (TR_out, A_BC_D_out, nABC_D_out, AB_CD_out, nA_BCD_out, ABCD_out, nABCD_out);
  nor BL (BL_out, A_B_C_D_out, AB_C_D_out, nA_BC_D_out, A_BC_D_out, ABC_D_out, A_B_CD_out);
  nor BR (BR_out, nAB_C_D_out, nABCD_out, nA_BCD_out, ABCD_out);
  _7_Segment_Display u_7_segment_display_1 (
    .g(Middle_out), .f(TL_out), .a(Top_out), .b(TR_out), .e(BL_out), .d(Bottom_out), .c(BR_out));  // open: dp
endmodule
