// Logisim project demux.circ as structural Verilog: 1 circuit, main circuit main
module main (
  input  sel,
  input  in
);

  wire and_1_out, and_2_out, not_1_out;

  not not_1 (not_1_out, sel);
  LED led_1 (.in(and_1_out));
  and and_1 (and_1_out, not_1_out, in);
  LED led_2 (.in(and_2_out));
  and and_2 (and_2_out, sel, in);
endmodule
