// Logisim project dmux4way.circ as structural Verilog: 1 circuit, main circuit main
module main (
  input  In,
  input  Sel_0,
  input  Sel_1
);

  wire and_1_out, and_2_out, and_3_out, and_4_out, and_5_out, and_6_out, and_7_out, and_8_out, not_1_out,
       not_2_out;

  not not_1 (not_1_out, Sel_0);
  not not_2 (not_2_out, Sel_1);
  and and_1 (and_1_out, not_1_out, not_2_out);
  and and_2 (and_2_out, Sel_0, not_2_out);
  and and_3 (and_3_out, not_1_out, Sel_1);
  and and_4 (and_4_out, Sel_0, Sel_1);
  LED A (.in(and_5_out));
  and and_5 (and_5_out, In, and_1_out);
  LED B (.in(and_6_out));
  and and_6 (and_6_out, In, and_2_out);
  and and_7 (and_7_out, In, and_3_out);
  LED C (.in(and_7_out));
  and and_8 (and_8_out, In, and_4_out);
  LED D (.in(and_8_out));
endmodule
