// Logisim project mux4way.circ as structural Verilog: 1 circuit, main circuit main
module main (
  input  A,
  input  B,
  input  C,
  input  D,
  input  Sel0,
  input  Sel1
);

  wire and_1_out, and_2_out, and_3_out, and_4_out, not_1_out, not_2_out, or_1_out, or_2_out, or_3_out,
       Sel_A_out, Sel_B_out, Sel_C_out, Sel_D_out;

  not not_1 (not_1_out, Sel0);
  not not_2 (not_2_out, Sel1);
  and Sel_A (Sel_A_out, not_1_out, not_2_out);
  and Sel_B (Sel_B_out, Sel0, not_2_out);
  and Sel_C (Sel_C_out, not_1_out, Sel1);
  and Sel_D (Sel_D_out, Sel0, Sel1);
  and and_1 (and_1_out, A, Sel_A_out);
  or or_1 (or_1_out, and_1_out, and_2_out);
  and and_2 (and_2_out, B, Sel_B_out);
  and and_3 (and_3_out, C, Sel_C_out);
  or or_2 (or_2_out, and_3_out, and_4_out);
  and and_4 (and_4_out, D, Sel_D_out);
  or or_3 (or_3_out, or_1_out, or_2_out);
  LED led_1 (.in(or_3_out));
endmodule
