// Logisim project not8.circ as structural Verilog: 1 circuit, main circuit main
module main (
  input  in_1,
  input  in_2,
  input  in_3,
  input  in_4,
  input  in_5,
  input  in_6,
  input  in_7,
  input  in_8
);

  wire nand_1_out, nand_2_out, nand_3_out, nand_4_out, nand_5_out, nand_6_out, nand_7_out, nand_8_out;

  nand nand_1 (nand_1_out, in_1, in_1);
  nand nand_2 (nand_2_out, in_2, in_2);
  nand nand_3 (nand_3_out, in_3, in_3);
  nand nand_4 (nand_4_out, in_4, in_4);
  nand nand_5 (nand_5_out, in_5, in_5);
  nand nand_6 (nand_6_out, in_6, in_6);
  nand nand_7 (nand_7_out, in_7, in_7);
  nand nand_8 (nand_8_out, in_8, in_8);
  LED led_1 (.in(nand_1_out));
  LED led_2 (.in(nand_2_out));
  LED led_3 (.in(nand_3_out));
  LED led_4 (.in(nand_4_out));
  LED led_5 (.in(nand_5_out));
  LED led_6 (.in(nand_6_out));
  LED led_7 (.in(nand_7_out));
  LED led_8 (.in(nand_8_out));
endmodule
