// Logisim project fulladder.circ as structural Verilog: 1 circuit, main circuit main
module main (
  input  A,
  input  B,
  input  C
);

  wire and_1_out, and_2_out, and_3_out, and_4_out, not_1_out, not_2_out, not_3_out, or_1_out, or_2_out,
       or_3_out, xnor_1_out, xor_1_out;

  not not_1 (not_1_out, A);
  not not_2 (not_2_out, B);
  not not_3 (not_3_out, C);
  xnor xnor_1 (xnor_1_out, A, B);
  and and_1 (and_1_out, xnor_1_out, C);
  or or_1 (or_1_out, A, B);
  and and_2 (and_2_out, or_1_out, C);
  and and_3 (and_3_out, A, B, not_3_out);
  xor xor_1 (xor_1_out, A, B);
  or or_2 (or_2_out, and_2_out, and_3_out);
  LED led_1 (.in(or_2_out));
  or or_3 (or_3_out, and_1_out, and_4_out);
  and and_4 (and_4_out, xor_1_out, not_3_out);
  LED led_2 (.in(or_3_out));
endmodule
