// Logisim project halfadder.circ as structural Verilog: 1 circuit, main circuit main
module main (
  input  A,
  input  B
);

  wire and_1_out, xor_1_out;

  LED Sum (.in(xor_1_out));
  xor xor_1 (xor_1_out, A, B);
  LED Carry (.in(and_1_out));
  and and_1 (and_1_out, A, B);
endmodule
