// Logisim project test.circ as structural Verilog: 2 circuits, main circuit main
module main (
  input  [15:0] in_1,
  input  [15:0] in_2
);
endmodule

module HalfAdder (
  input  in_1,
  input  in_2
);
endmodule
